# Fritzing sketch Arduino_Granular_Synth_Theremin (saved by Fritzing 0.9.10b)

parts:
  Εξάρτημα1 = Arduino Mega 2560 (Rev3)
  LED1 = LED - 5mm [color="Blue (525nm)" current=0.030 package="5 mm [THT]"]
  LED2 = LED - 5mm [color="Green (570nm)" current=0.030 package="5 mm [THT]"]
  LED3 = LED - 5mm [color="Red (633nm)" current=0.030 package="5 mm [THT]"]
  R1 = Rotary Potentiometer (Small) [maximum_resistance=10kΩ knob_status=50% power=0.5W package=THT]
  R2 = Rotary Potentiometer (Small) [maximum_resistance=10kΩ knob_status=50% power=0.5W package=THT]
  R3 = Rotary Potentiometer (Small) [maximum_resistance=10kΩ knob_status=50% power=0.5W package=THT]
  R4 = Rotary Potentiometer (Small) [maximum_resistance=10kΩ knob_status=50% power=0.5W package=THT]
  R5 = Rotary Potentiometer (Small) [maximum_resistance=10kΩ knob_status=50% power=0.5W package=THT]
  J1 = Infrared Proximity Sensor [distance_to_obstacle=50%]
  J2 = Infrared Proximity Sensor [distance_to_obstacle=50%]
  S1 = Toggle Switch [package=THT]
  S2 = Square Pushbutton
  R6 = Resistor [tolerance=±5% resistance=220 package="2512 [SMD]"]  # not connected
  R7 = Resistor [tolerance=±5% resistance=220 package="2512 [SMD]"]  # not connected
  R8 = Resistor [tolerance=±5% resistance=220 package="2512 [SMD]"]
  SP1 = SPEAKER [package=pcb_mount_speaker]
  R9 = Resistor [tolerance=±5% resistance=10k package="0402 [SMD]"]

nets:
  N1: Εξάρτημα1.A0, R4.wiper
  N2: Εξάρτημα1.A1, R2.wiper
  N3: Εξάρτημα1.A2, R5.wiper
  N4: Εξάρτημα1.A3, R1.wiper
  N5: Εξάρτημα1.A4, R3.wiper
  N6: Εξάρτημα1.A6, J1.Vout
  N7: Εξάρτημα1.A7, J2.Vout
  N8: Εξάρτημα1.GND, SP1.+
  N9: Εξάρτημα1.D10_PWM, LED2.anode
  N10: Εξάρτημα1.D9_PWM, LED1.anode
  N11: Εξάρτημα1.D8_PWM, LED3.anode
  N12: Εξάρτημα1.D2_PWM, S1.L2
  N13: Εξάρτημα1.D3_PWM, R9.Pin_1
  N14: Εξάρτημα1.D4_PWM, S1.L1
  N15: Εξάρτημα1.D6_PWM, S2.leg0
  N16: R1.leg2, J2.Vcc
  N17: R2.leg1, J1.GND
  N18: R4.leg1, R8.Pin_0
  N19: R4.leg2, J1.Vcc
  N20: J2.GND, S1.COM
